# Fritzing sketch SmartExhibitSchematic (saved by Fritzing 0.9.6b)
breadboards: 1

parts:
  Q1 = NPN-Transistor [part_number=2N2222 package="TO92 [THT]"]
  R1 = Resistor [tolerance=±5% power=0.6W resistance=220 package=THT]
  SPKR1 = Loudspeaker
  ARD = Arduino Nano 33 IOT
  SENSOR2 = DHT11 Humitidy and Temperature Sensor
  R2 = Resistor [tolerance=±5% power=0.25 resistance=5k package=THT]
  C1 = Ceramic Capacitor [capacitance=100nF voltage=35V package="100 mil [THT, multilayer]"]
  SENSOR1 = BH1750
  SENSOR3 = PIR sensor
  SENSOR4 = Adafruit MAX9814 Electret Microphone Amplifier [part_number=-]
  M1 = TP4056 Module [part_number=HW-107]
  U1 = LIPO-110mAh [package=lipo-110]
  PB1 = KY-004 Key Switch Module [package="Breakout board"]

nets:
  GND: Q1.E, ARD.GND, ARD.D13~, SENSOR2.GND, C1.0, SENSOR1.GND, SENSOR1.ADDR, SENSOR3.GND, SENSOR4.GND, M1.pin2, PB1.-
  N1: Q1.B, R1.Pin_1
  N2: Q1.C, SPKR1.pin2
  D3: R1.Pin_0, ARD.D3~
  3.7V: SPKR1.pin1, ARD.VIN, SENSOR2.VDD, R2.Pin_0, C1.1, SENSOR1.VCC, SENSOR3.VDD, SENSOR4.VDD, SENSOR4.GAIN, M1.pin5, PB1.Vin
  A7: ARD.RESET, ARD.A7, SENSOR4.OUTPUT
  D5: ARD.D5~, PB1.S
  D7: ARD.D7, SENSOR3.SIG
  D8: ARD.D8, SENSOR2.DATA
  N3: ARD.D11/MOSI, ARD.+5V
  SCL: ARD.A5, SENSOR1.SCL
  SDA: ARD.A4, SENSOR1.SDA
  N4: M1.pin3, U1.-
  N5: M1.pin4, U1.+

custom parts:
  Arduino Nano 33 IOT: The Arduino Nano 33 IoT is the easiest and cheapest point of entry to enhance existing devices (and creating new ones) to be part of the IoT and designing pico-network applications. Whether you are looking at building a sensor network connected to your office or home router, or if you want to create a BLE device sending data to a cellphone, the Nano 33 IoT is your one-stop-solution for many of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
  DHT11 Humitidy and Temperature Sensor: DHT11 Humidity and Temperature Sensor
  BH1750: Light Sensor
  Adafruit MAX9814 Electret Microphone Amplifier: Add an ear to your project with this well-designed electret microphone amplifier with AGC. This fully assembled and tested board comes with a 20-20KHz electret microphone soldered on. For the amplification, we use the Maxim MAX9814, a specialty chip that is designed for amplifying electret microphones in situations where the loudness of the audio isn't predictable. This fancy microphone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
  TP4056 Module: TP4056 Lithium Battery Charge Management Module Links: TP4056 website
  KY-004 Key Switch Module: Arduino Key Switch Module Keyes KY-004 is a push button that will output a high signal when pressed.
